# Fritzing sketch ESP8366Lora (saved by Fritzing 0.9.3b)
breadboards: 2

parts:
  WeMos_D1_Mini1 = WeMos D1 Mini
  Agge_LoRa_on_ESP-12F_breadbord1 = Agge LoRa on ESP-12F breadbord

nets:
  3V3: WeMos_D1_Mini1.3V3, Agge_LoRa_on_ESP-12F_breadbord1.3.3V
  N1: WeMos_D1_Mini1.D5, Agge_LoRa_on_ESP-12F_breadbord1.SCK
  N2: WeMos_D1_Mini1.D6, Agge_LoRa_on_ESP-12F_breadbord1.MISO
  N3: WeMos_D1_Mini1.D7, Agge_LoRa_on_ESP-12F_breadbord1.MOSI
  N4: WeMos_D1_Mini1.D8, Agge_LoRa_on_ESP-12F_breadbord1.NSS
  N5: WeMos_D1_Mini1.G, Agge_LoRa_on_ESP-12F_breadbord1.GND#8

custom parts:
  WeMos D1 Mini: The D1 mini is a mini wifi board based on ESP-8266EX.
