# Fritzing sketch ESP8366LoraOLED (saved by Fritzing 0.9.3b)
breadboards: 2

parts:
  WeMos_D1_Mini1 = WeMos D1 Mini
  Agge_LoRa_on_ESP-12F_breadbord1 = Agge LoRa on ESP-12F breadbord
  OLED1 = 128x64 Monochrom OLED Display with SPI Control

nets:
  3V3: WeMos_D1_Mini1.3V3, Agge_LoRa_on_ESP-12F_breadbord1.3.3V, OLED1.3v3
  N1: WeMos_D1_Mini1.D2, OLED1.SA0/DC
  N2: WeMos_D1_Mini1.D4, OLED1.CS
  N3: WeMos_D1_Mini1.D5, Agge_LoRa_on_ESP-12F_breadbord1.SCK, OLED1.Clock
  N4: WeMos_D1_Mini1.D6, Agge_LoRa_on_ESP-12F_breadbord1.MISO
  N5: WeMos_D1_Mini1.D7, Agge_LoRa_on_ESP-12F_breadbord1.MOSI, OLED1.Data
  N6: WeMos_D1_Mini1.D8, Agge_LoRa_on_ESP-12F_breadbord1.NSS
  N7: WeMos_D1_Mini1.G, Agge_LoRa_on_ESP-12F_breadbord1.GND#8, OLED1.GND

custom parts:
  WeMos D1 Mini: The D1 mini is a mini wifi board based on ESP-8266EX.
